# Fritzing sketch esquema (saved by Fritzing 0.9.3b)

parts:
  U1 = NodeMCU V3.0
  SparkFun_Particle_Sensor_Breakout_-_MAX1 = SparkFun MAX30105_Breakout [part_number=SEN-14045]

nets:
  N1: U1.D1, SparkFun_Particle_Sensor_Breakout_-_MAX1.SCL
  N2: U1.D2, SparkFun_Particle_Sensor_Breakout_-_MAX1.SDA
  3V3: U1.3V3, SparkFun_Particle_Sensor_Breakout_-_MAX1.5V
  GND: U1.GND, SparkFun_Particle_Sensor_Breakout_-_MAX1.GND

custom parts:
  NodeMCU V3.0: ESP8266 based NodeMCU
  SparkFun MAX30105_Breakout: Description: The SparkFun MAX30105 Particle Sensor is a flexible, powerful sensor enabling sensing of distance, heart rate, particle detection and even the blinking of an eye. The MAX30105 has been equipped with three LEDs as well as a very sensitive photon detector. The idea is to pulse the different LEDs, then detect what shines back. Based on the reflected signature it’s possible to detect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
